// Logisim project project.circ as structural Verilog: 21 circuits, main circuit main
module main (
);

  wire alu_1_eout, alu_1_selected, CLK, D0, D1, D2, D3, D4, D5, D6, D7, E, FGI, FGO, I, IEN,
       keyboard_1_avail, m_controler_1_lda, m_controler_1_str, R, s_1_s, T0, T1, T2, T3, T4, T5, T6, T7;
  wire [3:0] outr_1_out, outr_1_out_2;
  wire [6:0] keyboard_1_data;
  wire [7:0] INPR;
  wire [11:0] AR;
  wire [15:0] AC, alu_1_ac_2, BUS, DR, IR, M, PC, TR;

  IR ir_1 (
    .R(R), .T1(T1), .D(BUS), .CLK(CLK), .D0(D0), .D1(D1), .D2(D2), .D3(D3), .D4(D4), .D5(D5), .D6(D6),
    .D7(D7), .I(I), .BUS(IR));
  R r_1 (.FGI(FGI), .FGO(FGO), .IEN(IEN), .T0(T0), .T1(T1), .T2(T2), .CLK(CLK), .R(R));
  S s_1 (.CLK(CLK), .D7(D7), .I(I), .T3(T3), .IR(IR), .S(s_1_s));
  PC pc_1 (
    .T1(T1), .T2(T2), .T3(T3), .T4(T4), .T5(T5), .T6(T6), .D4(D4), .D5(D5), .D6(D6), .BUSin(BUS), .D7(D7),
    .I(I), .R(R), .AC(AC), .IR(IR), .E(E), .FGI(FGI), .FGO(FGO), .DR(DR), .CLK(CLK), .BUSout(PC));
  ALU alu_1 (
    .T3(T3), .T5(T5), .D0(D0), .D1(D1), .D2(D2), .D7(D7), .I(I), .IR(IR), .Ein(E), .DR(DR), .AC(AC),
    .INPR(INPR), .SELECTED(alu_1_selected), .Eout(alu_1_eout), .AC_2(alu_1_ac_2));
  BUS bus_1 (
    .T0(T0), .T1(T1), .T2(T2), .T3(T3), .T4(T4), .T5(T5), .T6(T6), .D0(D0), .D1(D1), .D2(D2), .D3(D3),
    .D4(D4), .D5(D5), .D6(D6), .D7(D7), .R(R), .I(I), .AR(AR), .PC(PC), .DR(DR), .AC(AC), .IR(IR), .TR(TR),
    .M(M), .BUS(BUS));
  SC sc_1 (
    .D0(D0), .D2(D2), .D3(D3), .D4(D4), .D5(D5), .D6(D6), .D7(D7), .R(R), .S(s_1_s), .CLK(CLK), .T0(T0),
    .T1(T1), .T2(T2), .T3(T3), .T4(T4), .T5(T5), .T6(T6), .T7(T7));  // open: T8, T9, T10, T11, T12, T13, T14, T15
  OUTR outr_1 (.D7(D7), .T3(T3), .I(I), .IR(IR), .BUSin(BUS), .CLK(CLK), .OUT({outr_1_out_2, outr_1_out}), .FGO(FGO));
  E e_1 (.D7(D7), .I(I), .T3(T3), .IR(IR), .D(alu_1_eout), .en(alu_1_selected), .CLK(CLK), .E(E));
  AC ac_1 (.T3(T3), .T5(T5), .D0(D0), .D1(D1), .D2(D2), .D7(D7), .I(I), .IR(IR), .D(alu_1_ac_2), .in_10(CLK), .BUS(AC));
  DR dr_1 (.D0(D0), .D1(D1), .D2(D2), .D6(D6), .T4(T4), .T5(T5), .BUSin(BUS), .CLK(CLK), .BUSout(DR));
  Hex_Digit_Display hex_digit_display_1 (.value(outr_1_out_2));  // open: dp
  AR ar_1 (.D7(D7), .I(I), .T3(T3), .T2(T2), .T0(T0), .D(BUS), .D5(D5), .T4(T4), .R(R), .BUS(AR), .CLK(CLK));
  Hex_Digit_Display hex_digit_display_2 (.value(outr_1_out));  // open: dp
  Clock clock_1 (.out(CLK));
  Keyboard keyboard_1 (.clk(CLK), .re(1'b1), .clr(1'b0), .avail(keyboard_1_avail), .data(keyboard_1_data));
  IEN ien_1 (.D7(D7), .I(I), .T3(T3), .R(R), .T2(T2), .IR(IR), .in_6(CLK), .IEN(IEN));
  TR tr_1 (.R(R), .T0(T0), .BUSin(BUS), .CLK(CLK), .BUSout(TR));
  M_controler m_controler_1 (
    .T1(T1), .T4(T4), .T6(T6), .D3(D3), .D5(D5), .D6(D6), .R(R), .STR(m_controler_1_str),
    .LDA(m_controler_1_lda));
  RAM #(.addrWidth(12), .dataWidth(16), .bus("separate")) ram_1 (
    .addr(AR), .din(BUS), .data(M), .str(m_controler_1_str), .sel(1'b1), .clk(CLK), .ld(m_controler_1_lda),
    .clr(1'b0));
  INPR inpr_1 (
    .Keyboard(keyboard_1_data), .FGI(keyboard_1_avail), .T3(T3), .I(I), .D7(D7), .IR(IR), .CLK(CLK),
    .FGI_2(FGI), .ALU(INPR));
endmodule

module half_adder (
  input  A,
  input  B,
  output S,
  output C
);

  xor xor_1 (S, A, B);
  and and_1 (C, A, B);
endmodule

// add 1
module full_bit_adder (
  input  A,
  input  Cin,
  input  B,
  output S,
  output Cout
);

  wire and_1_out, and_2_out, and_3_out, and_4_out, xor_1_out;

  and and_1 (and_1_out, B, Cin, A);
  and and_2 (and_2_out, Cin, B);
  or or_1 (Cout, and_2_out, and_3_out, and_4_out);
  and and_3 (and_3_out, A, B);
  and and_4 (and_4_out, A, Cin);
  ExactlyOne xor_1 (.out(xor_1_out), .in0(A), .in1(Cin), .in2(B));
  or or_2 (S, xor_1_out, and_1_out);
endmodule

// add 16
module adder_16 (
  input  A0,
  input  A1,
  input  A2,
  input  B3,
  input  A4,
  input  A5,
  input  A6,
  input  A7,
  input  A8,
  input  A9,
  input  A10,
  input  A11,
  input  A12,
  input  A13,
  input  A14,
  input  A15,
  input  B0,
  input  B1,
  input  B2,
  input  A3,
  input  B4,
  input  B5,
  input  B6,
  input  B7,
  input  B8,
  input  B9,
  input  B10,
  input  B11,
  input  B12,
  input  B13,
  input  B14,
  input  B15,
  output S0,
  output S1,
  output S2,
  output S3,
  output S4,
  output S5,
  output S6,
  output S7,
  output S8,
  output S9,
  output S10,
  output S11,
  output S12,
  output S13,
  output S14,
  output S15,
  output C16
);

  wire full_bit_adder_1_cout, full_bit_adder_2_cout, full_bit_adder_3_cout, full_bit_adder_4_cout,
       full_bit_adder_5_cout, full_bit_adder_6_cout, full_bit_adder_7_cout, full_bit_adder_8_cout,
       full_bit_adder_9_cout, full_bit_adder_10_cout, full_bit_adder_11_cout, full_bit_adder_12_cout,
       full_bit_adder_13_cout, full_bit_adder_14_cout, half_adder_1_c;

  half_adder half_adder_1 (.A(A0), .B(B0), .S(S0), .C(half_adder_1_c));
  full_bit_adder full_bit_adder_1 (.A(A1), .Cin(half_adder_1_c), .B(B1), .S(S1), .Cout(full_bit_adder_1_cout));
  full_bit_adder full_bit_adder_2 (.A(A2), .Cin(full_bit_adder_1_cout), .B(B2), .S(S2), .Cout(full_bit_adder_2_cout));
  full_bit_adder full_bit_adder_3 (.A(B3), .Cin(full_bit_adder_2_cout), .B(A3), .S(S3), .Cout(full_bit_adder_3_cout));
  full_bit_adder full_bit_adder_4 (.A(A4), .Cin(full_bit_adder_3_cout), .B(B4), .S(S4), .Cout(full_bit_adder_4_cout));
  full_bit_adder full_bit_adder_5 (.A(A5), .Cin(full_bit_adder_4_cout), .B(B5), .S(S5), .Cout(full_bit_adder_5_cout));
  full_bit_adder full_bit_adder_6 (.A(A6), .Cin(full_bit_adder_5_cout), .B(B6), .S(S6), .Cout(full_bit_adder_6_cout));
  full_bit_adder full_bit_adder_7 (.A(A7), .Cin(full_bit_adder_6_cout), .B(B7), .S(S7), .Cout(full_bit_adder_7_cout));
  full_bit_adder full_bit_adder_8 (.A(A8), .Cin(full_bit_adder_7_cout), .B(B8), .S(S8), .Cout(full_bit_adder_8_cout));
  full_bit_adder full_bit_adder_9 (.A(A9), .Cin(full_bit_adder_8_cout), .B(B9), .S(S9), .Cout(full_bit_adder_9_cout));
  full_bit_adder full_bit_adder_10 (
    .A(A10), .Cin(full_bit_adder_9_cout), .B(B10), .S(S10), .Cout(full_bit_adder_10_cout));
  full_bit_adder full_bit_adder_11 (
    .A(A11), .Cin(full_bit_adder_10_cout), .B(B11), .S(S11), .Cout(full_bit_adder_11_cout));
  full_bit_adder full_bit_adder_12 (
    .A(A12), .Cin(full_bit_adder_11_cout), .B(B12), .S(S12), .Cout(full_bit_adder_12_cout));
  full_bit_adder full_bit_adder_13 (
    .A(A13), .Cin(full_bit_adder_12_cout), .B(B13), .S(S13), .Cout(full_bit_adder_13_cout));
  full_bit_adder full_bit_adder_14 (
    .A(A14), .Cin(full_bit_adder_13_cout), .B(B14), .S(S14), .Cout(full_bit_adder_14_cout));
  full_bit_adder full_bit_adder_15 (.A(A15), .Cin(full_bit_adder_14_cout), .B(B15), .S(S15), .Cout(C16));
endmodule

module ALU (
  input  T3,
  input  T5,
  input  D0,
  input  D1,
  input  D2,
  input  D7,
  input  I,
  input  [15:0] IR,
  input  Ein,
  input  [15:0] DR,
  input  [15:0] AC,
  input  [7:0] INPR,
  output SELECTED,
  output Eout,
  output [15:0] AC_2
);

  wire ADD, adder_16_1_c16, AND, I_prime, NOT, r, SHL, SHR, T_DR, T_INPR;
  wire [2:0] SELECT;
  wire [15:0] adder_16_1_s0, and_1_out, not_2_out;

  not not_1 (I_prime, I);
  assign and_1_out = DR & AC;  // AND_Gate and_1, 16 bits wide
  assign not_2_out = ~AC;  // NOT_Gate not_2, 16 bits wide
  and and_2 (r, T3, D7, I_prime);
  and and_3 (AND, D0, T5);
  and and_4 (ADD, D1, T5);
  and and_5 (T_DR, D2, T5);
  adder_16 adder_16_1 (
    .A0(AC[0]), .A1(AC[1]), .A2(AC[2]), .B3(AC[3]), .A4(AC[4]), .A5(AC[5]), .A6(AC[6]), .A7(AC[7]),
    .A8(AC[8]), .A9(AC[9]), .A10(AC[10]), .A11(AC[11]), .A12(AC[12]), .A13(AC[13]), .A14(AC[14]),
    .A15(AC[15]), .B0(DR[0]), .B1(DR[1]), .B2(DR[2]), .A3(DR[3]), .B4(DR[4]), .B5(DR[5]), .B6(DR[6]),
    .B7(DR[7]), .B8(DR[8]), .B9(DR[9]), .B10(DR[10]), .B11(DR[11]), .B12(DR[12]), .B13(DR[13]), .B14(DR[14]),
    .B15(DR[15]), .S0(adder_16_1_s0[0]), .S1(adder_16_1_s0[1]), .S2(adder_16_1_s0[2]), .S3(adder_16_1_s0[3]),
    .S4(adder_16_1_s0[4]), .S5(adder_16_1_s0[5]), .S6(adder_16_1_s0[6]), .S7(adder_16_1_s0[7]),
    .S8(adder_16_1_s0[8]), .S9(adder_16_1_s0[9]), .S10(adder_16_1_s0[10]), .S11(adder_16_1_s0[11]),
    .S12(adder_16_1_s0[12]), .S13(adder_16_1_s0[13]), .S14(adder_16_1_s0[14]), .S15(adder_16_1_s0[15]),
    .C16(adder_16_1_c16));
  and and_6 (NOT, r, IR[9]);
  and and_7 (SHR, r, IR[7]);
  and and_8 (SHL, r, IR[6]);
  and and_9 (T_INPR, T3, D7, I, IR[11]);
  Priority_Encoder priority_encoder_1 (
    .in0(1'b0), .in1(SHL), .in2(SHR), .in3(ADD), .in4(AND), .in5(NOT), .in6(T_DR), .in7(T_INPR),
    .out(SELECT), .en_in(1'b1), .gs(SELECTED));  // open: en_out
  Multiplexer #(.select(3)) multiplexer_1 (
    .in1(AC[15]), .in2(AC[0]), .in3(adder_16_1_c16), .in4(Ein), .in5(Ein), .in6(Ein), .in7(Ein), .out(Eout),
    .sel(SELECT), .en(1'b1));  // open: in0
  Multiplexer #(.select(3), .width(16)) multiplexer_2 (
    .in1({AC[14:0], Ein}), .in2({Ein, AC[15:1]}), .in3(adder_16_1_s0), .in4(and_1_out), .in5(not_2_out),
    .in6(DR), .in7({{8{1'b0}}, INPR}), .out(AC_2), .sel(SELECT), .en(1'b1));  // open: in0

  // Other names for the same wires on the sheet: B5 = IR[5]; B6 = IR[6]; B7 = IR[7]; B9 = IR[9]; B11 = IR[11]

  // Notes on the sheet:
  //   SHL
  //   SHR
endmodule

module AC (
  input  T3,
  input  T5,
  input  D0,
  input  D1,
  input  D2,
  input  D7,
  input  I,
  input  [15:0] IR,
  input  [15:0] D,
  input  in_10,
  output [15:0] BUS
);

  wire and_2_out, and_3_out, and_4_out, and_5_out, and_6_out, I_prime, or_1_out, or_2_out, or_3_out, r;

  not not_1 (I_prime, I);
  and and_1 (r, T3, D7, I_prime);
  or or_1 (or_1_out, D0, D1, D2);
  and and_2 (and_2_out, T5, or_1_out);
  and and_3 (and_3_out, T3, D7, I, IR[11]);
  or or_2 (or_2_out, and_2_out, and_3_out, and_6_out);
  Counter #(.width(16), .max('hffff)) AC (
    .load(or_2_out), .D(D), .count(and_4_out), .Q(BUS), .clk(in_10), .clr(and_5_out));  // open: carry
  and and_4 (and_4_out, r, IR[5]);
  and and_5 (and_5_out, r, IR[11]);
  and and_6 (and_6_out, r, or_3_out);
  or or_3 (or_3_out, IR[9], IR[7], IR[6]);

  // Other names for the same wires on the sheet: B5 = IR[5]; B6 = IR[6]; B7 = IR[7]; B9 = IR[9]; B11 = IR[11]
endmodule

module IR (
  input  R,
  input  T1,
  input  [15:0] D,
  input  CLK,
  output D0,
  output D1,
  output D2,
  output D3,
  output D4,
  output D5,
  output D6,
  output D7,
  output I,
  output [15:0] BUS
);

  wire and_1_out, not_1_out;

  not not_1 (not_1_out, R);
  and and_1 (and_1_out, not_1_out, T1);
  Decoder #(.select(3)) decoder_1 (
    .out0(D0), .out1(D1), .out2(D2), .out3(D3), .out4(D4), .out5(D5), .out6(D6), .out7(D7), .sel(BUS[14:12]),
    .en(1'b1));
  Counter #(.width(16), .max('hffff)) IR (
    .load(and_1_out), .D(D), .count(1'b0), .Q(BUS), .clk(CLK), .clr(1'b0));  // open: carry
  D_Flip_Flop d_ff_1 (.clk(CLK), .D(BUS[15]), .Q(I), .preset(1'b0), .en(1'b1), .reset(1'b0));  // open: Qn
endmodule

module AR (
  input  D7,
  input  I,
  input  T3,
  input  T2,
  input  T0,
  input  [15:0] D,
  input  D5,
  input  T4,
  input  R,
  input  CLK,
  output [11:0] BUS
);

  wire and_1_out, and_2_out, and_3_out, and_4_out, not_1_out, not_2_out, or_1_out, or_2_out;

  not not_1 (not_1_out, D7);
  or or_1 (or_1_out, T2, T0);
  not not_2 (not_2_out, R);
  and and_1 (and_1_out, T0, R);
  and and_2 (and_2_out, not_1_out, I, T3);
  and and_3 (and_3_out, or_1_out, not_2_out);
  and and_4 (and_4_out, D5, T4);
  or or_2 (or_2_out, and_2_out, and_3_out);
  Counter #(.width(12), .max('hfff)) AR (
    .load(or_2_out), .D(D[11:0]), .count(and_4_out), .Q(BUS), .clk(CLK), .clr(and_1_out));  // open: carry
endmodule

module PC (
  input  T1,
  input  T2,
  input  T3,
  input  T4,
  input  T5,
  input  T6,
  input  D4,
  input  D5,
  input  D6,
  input  [15:0] BUSin,
  input  D7,
  input  I,
  input  CLK,
  input  R,
  input  [15:0] AC,
  input  [15:0] IR,
  input  E,
  input  FGI,
  input  FGO,
  input  [15:0] DR,
  output [15:0] BUSout
);

  wire AC_0, and_1_out, and_2_out, and_3_out, and_4_out, and_5_out, and_6_out, and_7_out, and_8_out,
       and_9_out, and_10_out, and_11_out, and_12_out, DR_0, not_1_out, not_2_out, not_3_out, or_1_out,
       or_2_out, p, R_prime, r_t;

  not not_1 (not_1_out, AC[15]);
  not not_2 (not_2_out, E);
  and and_1 (and_1_out, R_prime, T1);
  and and_2 (and_2_out, R, T2);
  and and_3 (and_3_out, D6, T6, DR_0);
  and and_4 (and_4_out, r_t, IR[4], not_1_out);
  and and_5 (and_5_out, r_t, IR[3], AC[15]);
  and and_6 (and_6_out, r_t, IR[2], AC_0);
  and and_7 (and_7_out, r_t, IR[1], not_2_out);
  and and_8 (and_8_out, p, IR[9], FGI);
  and and_9 (and_9_out, FGO, p, IR[8]);
  and and_10 (and_10_out, D4, T4);
  and and_11 (and_11_out, D5, T5);
  or or_1 (or_1_out, and_1_out, and_2_out, and_3_out, and_4_out, and_5_out, and_6_out, and_7_out, and_8_out, and_9_out);
  or or_2 (or_2_out, and_10_out, and_11_out);
  Counter #(.width(16), .max('hffff)) PC (
    .load(or_2_out), .D(BUSin), .count(or_1_out), .Q(BUSout), .clk(CLK), .clr(and_12_out));  // open: carry
  and and_12 (and_12_out, R, T1);
  not not_3 (not_3_out, I);
  not not_4 (R_prime, R);
  and and_13 (p, D7, T3, I);
  and and_14 (r_t, not_3_out, D7, T3);
  nor nor_1 (AC_0, AC[0], AC[1], AC[2], AC[3], AC[4], AC[5], AC[6], AC[7], AC[8], AC[9], AC[10], AC[11], AC[12], AC[13], AC[14], AC[15]);
  nor nor_2 (DR_0, DR[0], DR[1], DR[2], DR[3], DR[4], DR[5], DR[6], DR[7], DR[8], DR[9], DR[10], DR[11], DR[12], DR[13], DR[14], DR[15]);
endmodule

module DR (
  input  D0,
  input  D1,
  input  D2,
  input  D6,
  input  T4,
  input  T5,
  input  [15:0] BUSin,
  input  CLK,
  output [15:0] BUSout
);

  wire and_1_out, and_2_out, or_1_out;

  or or_1 (or_1_out, D0, D1, D2, D6);
  and and_1 (and_1_out, D6, T5);
  and and_2 (and_2_out, or_1_out, T4);
  Counter #(.width(16), .max('hffff)) DR (
    .load(and_2_out), .D(BUSin), .count(and_1_out), .Q(BUSout), .clk(CLK), .clr(1'b0));  // open: carry
endmodule

module TR (
  input  R,
  input  T0,
  input  [15:0] BUSin,
  input  CLK,
  output [15:0] BUSout
);

  wire and_1_out;

  and and_1 (and_1_out, R, T0);
  Counter #(.width(16), .max('hffff)) TR (
    .load(and_1_out), .D(BUSin), .count(1'b0), .Q(BUSout), .clk(CLK), .clr(1'b0));  // open: carry
endmodule

module OUTR (
  input  D7,
  input  T3,
  input  I,
  input  [15:0] IR,
  input  [15:0] BUSin,
  input  CLK,
  output [7:0] OUT,
  output FGO
);

  wire and_1_out;

  and and_1 (and_1_out, D7, T3, I, IR[10]);
  Counter counter_1 (.load(and_1_out), .D(BUSin[7:0]), .count(1'b0), .Q(OUT), .clk(CLK), .clr(1'b0));  // open: carry
  D_Flip_Flop d_ff_1 (.clk(CLK), .D(1'b1), .Q(FGO), .preset(1'b0), .en(1'b1), .reset(1'b0));  // open: Qn
endmodule

module INPR (
  input  [6:0] Keyboard,
  input  FGI,
  input  T3,
  input  I,
  input  D7,
  input  [15:0] IR,
  input  CLK,
  output FGI_2,
  output [7:0] ALU
);

  wire and_1_out, not_1_out, not_2_out, not_3_out, or_1_out, PB11;

  not not_1 (not_1_out, PB11);
  and and_1 (and_1_out, FGI, not_1_out);
  and and_2 (PB11, T3, I, D7, IR[11]);
  or or_1 (or_1_out, PB11, not_2_out);
  D_Flip_Flop d_ff_1 (.clk(CLK), .D(and_1_out), .Q(FGI_2), .preset(1'b0), .en(or_1_out), .reset(1'b0));  // open: Qn
  not not_2 (not_2_out, FGI_2);
  not not_3 (not_3_out, FGI_2);
  Counter counter_1 (
    .load(not_3_out), .D({1'b0, Keyboard}), .count(1'b0), .Q(ALU), .clk(CLK), .clr(1'b0));  // open: carry
endmodule

module SC (
  input  D0,
  input  D2,
  input  D3,
  input  D4,
  input  D5,
  input  D6,
  input  D7,
  input  R,
  input  S,
  input  CLK,
  output T0,
  output T1,
  output T2,
  output T3,
  output T4,
  output T5,
  output T6,
  output T7,
  output T8,
  output T9,
  output T10,
  output T11,
  output T12,
  output T13,
  output T14,
  output T15
);

  wire and_1_out, and_2_out, and_3_out, and_4_out, and_5_out, nor_1_out, not_1_out, not_2_out, or_1_out,
       or_2_out;
  wire [3:0] counter_1_q;

  and and_1 (and_1_out, T2, R);
  not not_1 (not_1_out, nor_1_out);
  nor nor_1 (nor_1_out, and_1_out, and_3_out, and_2_out, and_4_out, and_5_out, not_2_out);
  and and_2 (and_2_out, T4, or_1_out);
  and and_3 (and_3_out, T3, D7);
  or or_1 (or_1_out, D3, D4);
  Counter #(.width(4), .max('hf)) counter_1 (
    .load(not_1_out), .D(4'b0000), .count(nor_1_out), .Q(counter_1_q), .clk(CLK));  // open: carry, clr
  Decoder #(.select(4), .enable("false")) decoder_1 (
    .out0(T0), .out1(T1), .out2(T2), .out3(T3), .out4(T4), .out5(T5), .out6(T6), .out7(T7), .out8(T8),
    .out9(T9), .out10(T10), .out11(T11), .out12(T12), .out13(T13), .out14(T14), .out15(T15), .sel(counter_1_q));
  and and_4 (and_4_out, T5, or_2_out);
  or or_2 (or_2_out, D0, D2, D4, D5);
  and and_5 (and_5_out, T6, D6);
  not not_2 (not_2_out, S);
endmodule

module S (
  input  CLK,
  input  D7,
  input  I,
  input  T3,
  input  [15:0] IR,
  output S
);

  wire and_1_out, not_1_out, s_r_ff_1_qn;

  not not_1 (not_1_out, I);
  and and_1 (and_1_out, D7, not_1_out, T3, IR[0]);
  S_R_Flip_Flop s_r_ff_1 (.S(and_1_out), .clk(CLK), .R(1'b0), .Qn(s_r_ff_1_qn));  // open: Q, preset, reset, en
  D_Flip_Flop d_ff_1 (.clk(CLK), .D(s_r_ff_1_qn), .Q(S), .preset(1'b0), .en(1'b1), .reset(1'b0));  // open: Qn
endmodule

module IEN (
  input  D7,
  input  I,
  input  T3,
  input  R,
  input  T2,
  input  in_6,
  input  [15:0] IR,
  output IEN
);

  wire and_1_out, and_2_out, and_3_out, and_4_out, or_1_out;

  and and_1 (and_1_out, D7, I, T3);
  and and_2 (and_2_out, and_1_out, IR[6]);
  and and_3 (and_3_out, R, T2);
  and and_4 (and_4_out, and_1_out, IR[7]);
  or or_1 (or_1_out, and_2_out, and_3_out);
  J_K_Flip_Flop j_k_ff_1 (
    .J(and_4_out), .clk(in_6), .K(or_1_out), .Q(IEN), .preset(1'b0), .en(1'b1), .reset(1'b0));  // open: Qn
endmodule

module I (
  input  [15:0] IR,
  input  R,
  input  T2,
  output I
);

  wire and_1_out, and_2_out, not_1_out, not_2_out;

  not not_1 (not_1_out, R);
  not not_2 (not_2_out, IR[15]);
  and and_1 (and_1_out, IR[15], not_1_out, T2);
  and and_2 (and_2_out, T2, not_1_out, not_2_out);
  J_K_Flip_Flop j_k_ff_1 (
    .J(and_1_out), .K(and_2_out), .Q(I), .preset(1'b0), .en(1'b1), .reset(1'b0));  // open: clk, Qn
endmodule

module E (
  input  D7,
  input  I,
  input  T3,
  input  [15:0] IR,
  input  D,
  input  en,
  input  CLK,
  output E
);

  wire and_2_out, and_3_out, and_4_out, and_5_out, not_1_out, not_2_out, or_1_out, or_2_out, or_3_out, r;

  not not_1 (not_1_out, D);
  not not_2 (not_2_out, I);
  and and_1 (r, D7, not_2_out, T3);
  and and_2 (and_2_out, D, en);
  and and_3 (and_3_out, en, not_1_out);
  and and_4 (and_4_out, r, or_1_out);
  or or_1 (or_1_out, IR[8], IR[10]);
  or or_2 (or_2_out, and_2_out, and_5_out);
  and and_5 (and_5_out, r, IR[8]);
  or or_3 (or_3_out, and_4_out, and_3_out);
  J_K_Flip_Flop j_k_ff_1 (
    .J(or_2_out), .clk(CLK), .K(or_3_out), .Q(E), .preset(1'b0), .en(1'b1), .reset(1'b0));  // open: Qn

  // Other names for the same wires on the sheet: B8 = IR[8]; B10 = IR[10]
endmodule

module R (
  input  FGI,
  input  FGO,
  input  IEN,
  input  T0,
  input  T1,
  input  T2,
  input  CLK,
  output R
);

  wire and_1_out, and_2_out, not_1_out, not_2_out, not_3_out, or_1_out;

  or or_1 (or_1_out, FGI, FGO);
  not not_1 (not_1_out, T0);
  not not_2 (not_2_out, T1);
  not not_3 (not_3_out, T2);
  and and_1 (and_1_out, or_1_out, IEN, not_1_out, not_2_out, not_3_out);
  and and_2 (and_2_out, T2, R);
  J_K_Flip_Flop j_k_ff_1 (
    .J(and_1_out), .clk(CLK), .K(and_2_out), .Q(R), .preset(1'b0), .en(1'b1), .reset(1'b0));  // open: Qn
endmodule

module BUS (
  input  T0,
  input  T1,
  input  T2,
  input  T3,
  input  T4,
  input  T5,
  input  T6,
  input  D0,
  input  D1,
  input  D2,
  input  D3,
  input  D4,
  input  D5,
  input  D6,
  input  D7,
  input  R,
  input  I,
  input  [11:0] AR,
  input  [15:0] PC,
  input  [15:0] DR,
  input  [15:0] AC,
  input  [15:0] IR,
  input  [15:0] TR,
  input  [15:0] M,
  output [15:0] BUS
);

  wire and_1_out, and_2_out, and_3_out, and_4_out, and_5_out, and_6_out, and_7_out, and_8_out, and_9_out,
       and_10_out, and_11_out, D7_prime, or_1_out, or_2_out, or_3_out, or_4_out, or_5_out, R_prime;
  wire [2:0] priority_encoder_1_out;

  not not_1 (D7_prime, D7);
  not not_2 (R_prime, R);
  and and_1 (and_1_out, T4, D4);
  or or_1 (or_1_out, and_1_out, and_2_out);
  and and_2 (and_2_out, T5, D5);
  or or_2 (or_2_out, T0, and_3_out);
  and and_3 (and_3_out, D5, T4);
  and and_4 (and_4_out, T6, D6);
  and and_5 (and_5_out, T4, D3);
  or or_3 (or_3_out, and_5_out, and_6_out);
  and and_6 (and_6_out, D7, I, T3, IR[10]);
  and and_7 (and_7_out, R_prime, T2);
  and and_8 (and_8_out, T1, R);
  or or_4 (or_4_out, and_9_out, and_10_out, and_11_out);
  and and_9 (and_9_out, R_prime, T1);
  and and_10 (and_10_out, T3, I, D7_prime);
  Priority_Encoder priority_encoder_1 (
    .in1(or_1_out), .in2(or_2_out), .in3(and_4_out), .in4(or_3_out), .in5(and_7_out), .in6(and_8_out),
    .in7(or_4_out), .out(priority_encoder_1_out), .en_in(1'b1));  // open: in0, gs, en_out
  and and_11 (and_11_out, T4, or_5_out);
  or or_5 (or_5_out, D0, D1, D2, D6);
  Multiplexer #(.select(3), .width(16)) multiplexer_1 (
    .in1({4'b0000, AR}), .in2(PC), .in3(DR), .in4(AC), .in5(IR), .in6(TR), .in7(M), .out(BUS),
    .sel(priority_encoder_1_out), .en(1'b1));  // open: in0

  // Other names for the same wires on the sheet: B10 = IR[10]
endmodule

module M_controler (
  input  T1,
  input  T4,
  input  T6,
  input  D3,
  input  D5,
  input  D6,
  input  R,
  output STR,
  output LDA
);

  wire and_1_out, and_2_out, and_3_out, or_1_out;

  or or_1 (or_1_out, D3, D5);
  and and_1 (and_1_out, R, T1);
  and and_2 (and_2_out, or_1_out, T4);
  and and_3 (and_3_out, D6, T6);
  not not_1 (STR, LDA);
  nor nor_1 (LDA, and_1_out, and_2_out, and_3_out);
endmodule
